// Logisim project sqrt2.circ as structural Verilog: 20 circuits, main circuit main
module main (
  input  ENABLE,
  input  [15:0] IO_DATA_IN,
  output NAN,
  output PINF,
  output NINF,
  output RESULT,
  output [15:0] IO_DATA_OUT
);

  wire CLK_out;

  Clock CLK (.out(CLK_out));
  sqrt sqrt_1 (
    .CLK(CLK_out), .ENABLE(ENABLE), .IO_DATA_IN(IO_DATA_IN), .IS_NAN(NAN), .IS_PINF(PINF), .IS_NINF(NINF),
    .RESULT(RESULT), .IO_DATA_OUT(IO_DATA_OUT));
endmodule

module sqrt (
  input  CLK,
  input  ENABLE,
  input  [15:0] IO_DATA_IN,
  output IS_NAN,
  output IS_PINF,
  output IS_NINF,
  output RESULT,
  output [15:0] IO_DATA_OUT
);


  assign IO_DATA_OUT = IO_DATA_IN;
endmodule

module sum1 (
  input  A,
  input  B,
  input  Cin,
  output S,
  output Cout
);

  wire and_1_out, and_2_out, xor_1_out;

  xor xor_1 (xor_1_out, A, B);
  xor xor_2 (S, xor_1_out, Cin);
  and and_1 (and_1_out, xor_1_out, Cin);
  and and_2 (and_2_out, A, B);
  or or_1 (Cout, and_1_out, and_2_out);
endmodule

module sum2 (
  input  [1:0] A,
  input  [1:0] B,
  input  Cin,
  output [1:0] S,
  output Cout
);

  wire sum1_1_cout;

  sum1 sum1_1 (.A(A[0]), .B(B[0]), .Cin(Cin), .S(S[0]), .Cout(sum1_1_cout));
  sum1 sum1_2 (.A(A[1]), .B(B[1]), .Cin(sum1_1_cout), .S(S[1]), .Cout(Cout));
endmodule

module sum4 (
  input  [3:0] A,
  input  [3:0] B,
  input  Cin,
  output [3:0] S,
  output Cout
);

  wire sum2_1_cout;

  sum2 sum2_1 (.A(A[1:0]), .B(B[1:0]), .Cin(Cin), .S(S[1:0]), .Cout(sum2_1_cout));
  sum2 sum2_2 (.A(A[3:2]), .B(B[3:2]), .Cin(sum2_1_cout), .S(S[3:2]), .Cout(Cout));

  // Other names for the same wires on the sheet: A1[1:0] = A[3:2]; B1[1:0] = B[3:2]
endmodule

module sum8 (
  input  [7:0] A,
  input  [7:0] B,
  input  Cin,
  output [7:0] S,
  output Cout
);

  wire sum4_1_cout;

  sum4 sum4_1 (.A(A[3:0]), .B(B[3:0]), .Cin(Cin), .S(S[3:0]), .Cout(sum4_1_cout));
  sum4 sum4_2 (.A(A[7:4]), .B(B[7:4]), .Cin(sum4_1_cout), .S(S[7:4]), .Cout(Cout));

  // Other names for the same wires on the sheet: A1[3:0] = A[7:4]; B1[3:0] = B[7:4]
endmodule

module sum16 (
  input  [15:0] A,
  input  [15:0] B,
  input  Cin,
  output [15:0] S,
  output Cout
);

  wire sum8_1_cout;

  sum8 sum8_1 (.A(A[7:0]), .B(B[7:0]), .Cin(Cin), .S(S[7:0]), .Cout(sum8_1_cout));
  sum8 sum8_2 (.A(A[15:8]), .B(B[15:8]), .Cin(sum8_1_cout), .S(S[15:8]), .Cout(Cout));

  // Other names for the same wires on the sheet: A1[7:0] = A[15:8]; B1[7:0] = B[15:8]
endmodule

module sum32 (
  input  [31:0] A,
  input  [31:0] B,
  input  Cin,
  output [31:0] S,
  output Cout
);

  wire sum16_1_cout;

  sum16 sum16_1 (.A(A[15:0]), .B(B[15:0]), .Cin(Cin), .S(S[15:0]), .Cout(sum16_1_cout));
  sum16 sum16_2 (.A(A[31:16]), .B(B[31:16]), .Cin(sum16_1_cout), .S(S[31:16]), .Cout(Cout));

  // Other names for the same wires on the sheet: A1[15:0] = A[31:16]; B1[15:0] = B[31:16]
endmodule

module input_parser (
  input  [15:0] N,
  input  Clk,
  input  Load,
  output [9:0] Mant,
  output [4:0] Exp,
  output IS_ZERO,
  output IS_DENORM,
  output IS_NAN,
  output Sign,
  output IS_INF
);

  wire and_1_out, M_0, M_NOT_0, nor_2_out;

  nor nor_1 (M_0, N[0], N[1], N[2], N[3], N[4], N[5], N[6], N[7], N[8], N[9]);
  nor nor_2 (nor_2_out, N[10], N[11], N[12], N[13], N[14]);
  and and_1 (and_1_out, N[10], N[11], N[12], N[13], N[14]);
  not not_1 (M_NOT_0, M_0);
  // Probe on nor_2_out
  // Probe on and_1_out
  // Probe on M_NOT_0
  // Probe on M_0
  and and_2 (IS_ZERO, nor_2_out, M_0);
  and and_3 (IS_DENORM, nor_2_out, M_NOT_0);
  and and_4 (IS_NAN, M_NOT_0, and_1_out);
  and and_5 (IS_INF, M_0, and_1_out);

  assign Exp = N[14:10];
  assign Mant = N[9:0];
  assign Sign = N[15];
endmodule

module right_shift (
  input  [31:0] in_1,
  output OutBit,
  output [31:0] Res
);


  assign OutBit = in_1[0];
  assign Res = {1'b0, in_1[31:1]};
endmodule

module left_shift (
  input  [31:0] in_1,
  output [31:0] Res,
  output OutBit
);


  assign OutBit = in_1[31];
  assign Res = {in_1[30:0], 1'b0};
endmodule

module special_case_handler (
  input  [9:0] Mant,
  input  [4:0] Exp,
  input  IS_DENORM,
  input  Sign,
  input  IS_ZERO,
  input  IS_NAN,
  input  IS_INF,
  output SPECIAL_OUT,
  output BYPASS_CORE
);

  wire and_1_out, not_1_out;

  not not_1 (not_1_out, IS_ZERO);
  and and_1 (and_1_out, Sign, not_1_out);
  or or_1 (BYPASS_CORE, and_1_out, IS_ZERO, IS_NAN, IS_INF);
endmodule

module mux_2_1 (
  input  D1,
  input  D0,
  input  COND,
  output RES
);

  wire and_1_out, and_2_out, not_1_out;

  not not_1 (not_1_out, COND);
  and and_1 (and_1_out, D1, COND);
  and and_2 (and_2_out, D0, not_1_out);
  or or_1 (RES, and_1_out, and_2_out);
endmodule

module mux_4_1 (
  input  D3,
  input  D2,
  input  D1,
  input  D0,
  input  S0,
  input  S1,
  output RES
);

  wire mux_2_1_1_res, mux_2_1_2_res;

  mux_2_1 mux_2_1_1 (.D1(D3), .D0(D2), .COND(S0), .RES(mux_2_1_1_res));
  mux_2_1 mux_2_1_2 (.D1(D1), .D0(D0), .COND(S0), .RES(mux_2_1_2_res));
  mux_2_1 mux_2_1_3 (.D1(mux_2_1_1_res), .D0(mux_2_1_2_res), .COND(S1), .RES(RES));
endmodule

module mux_8_1 (
  input  D7,
  input  D6,
  input  D5,
  input  D4,
  input  D3,
  input  D2,
  input  D1,
  input  D0,
  input  S0,
  input  S1,
  input  S2,
  output RES
);

  wire mux_4_1_1_res, mux_4_1_2_res;

  mux_4_1 mux_4_1_1 (.D3(D7), .D2(D6), .D1(D5), .D0(D4), .S0(S0), .S1(S1), .RES(mux_4_1_1_res));
  mux_4_1 mux_4_1_2 (.D3(D3), .D2(D2), .D1(D1), .D0(D0), .S0(S0), .S1(S1), .RES(mux_4_1_2_res));
  mux_2_1 mux_2_1_1 (.D1(mux_4_1_1_res), .D0(mux_4_1_2_res), .COND(S2), .RES(RES));
endmodule

module mux_2_1_2bit (
  input  [1:0] D1,
  input  [1:0] D0,
  input  COND,
  output [1:0] RES
);

  mux_2_1 mux_2_1_1 (.D1(D1[0]), .D0(D0[0]), .COND(COND), .RES(RES[0]));
  mux_2_1 mux_2_1_2 (.D1(D1[1]), .D0(D0[1]), .COND(COND), .RES(RES[1]));
endmodule

module mux_2_1_4bit (
  input  [3:0] D1,
  input  [3:0] D0,
  input  COND,
  output [3:0] RES
);

  mux_2_1_2bit mux_2_1_2bit_1 (.D1(D1[1:0]), .D0(D0[1:0]), .COND(COND), .RES(RES[1:0]));
  mux_2_1_2bit mux_2_1_2bit_2 (.D1(D1[3:2]), .D0(D0[3:2]), .COND(COND), .RES(RES[3:2]));
endmodule

module mux_2_1_8bit (
  input  [7:0] D1,
  input  [7:0] D0,
  input  COND,
  output [7:0] RES
);

  mux_2_1_4bit mux_2_1_4bit_1 (.D1(D1[3:0]), .D0(D0[3:0]), .COND(COND), .RES(RES[3:0]));
  mux_2_1_4bit mux_2_1_4bit_2 (.D1(D1[7:4]), .D0(D0[7:4]), .COND(COND), .RES(RES[7:4]));
endmodule

module mux_2_1_16bit (
  input  [15:0] D1,
  input  [15:0] D0,
  input  COND,
  output [15:0] RES
);

  mux_2_1_8bit mux_2_1_8bit_1 (.D1(D1[7:0]), .D0(D0[7:0]), .COND(COND), .RES(RES[7:0]));
  mux_2_1_8bit mux_2_1_8bit_2 (.D1(D1[15:8]), .D0(D0[15:8]), .COND(COND), .RES(RES[15:8]));
endmodule

module mux_4_1_16bit (
  input  [15:0] D3,
  input  [15:0] D2,
  input  [15:0] D1,
  input  [15:0] D0,
  input  S0,
  input  S1,
  output [15:0] RES
);

  wire [15:0] mux_2_1_16bit_1_res, mux_2_1_16bit_2_res;

  mux_2_1_16bit mux_2_1_16bit_1 (.D1(D3), .D0(D2), .COND(S0), .RES(mux_2_1_16bit_1_res));
  mux_2_1_16bit mux_2_1_16bit_2 (.D1(D1), .D0(D0), .COND(S0), .RES(mux_2_1_16bit_2_res));
  mux_2_1_16bit mux_2_1_16bit_3 (.D1(mux_2_1_16bit_1_res), .D0(mux_2_1_16bit_2_res), .COND(S1), .RES(RES));
endmodule
